// Logisim project ALU32.circ as structural Verilog: 7 circuits, main circuit ALU
// lessthan32
module ALU (
  input  [3:0] Op,
  input  [31:0] A,
  input  [31:0] B,
  input  in_4,
  input  [4:0] Shamt,
  output V,
  output [31:0] Output
);

  wire add_sub32_out_5, not_1_out;
  wire [31:0] add_sub32_output, AND32_out, equal32_output, greaterthan32_out_2, lessthan32_out_2,
       multiplexer_1_out, multiplexer_2_out, multiplexer_3_out, multiplexer_4_out, NOR32_out,
       notequal32_out_3, OR32_out, shifter32_output, XOR32_out;

  not not_1 (not_1_out, Op[3]);
  ADDSUB32 add_sub32 (.A(A), .in_2(Op[2]), .B(B), .out_5(add_sub32_out_5), .\output (add_sub32_output));
  and and_1 (V, not_1_out, add_sub32_out_5, Op[1]);
  SHIFTER32 shifter32 (.Cin(in_4), .A(B), .shamt(Shamt), .cntrl({Op[2], Op[0]}), .\output (shifter32_output));
  EQUAL32 equal32 (.A(A), .B(B), .\output (equal32_output));
  NOTEQUAL32 notequal32 (.A(A), .B(B), .out_3(notequal32_out_3));
  GREATERTHAN32 greaterthan32 (.in_1(A), .out_2(greaterthan32_out_2));
  LESSTHAN32 lessthan32 (.A(A), .out_2(lessthan32_out_2));
  assign AND32_out = A & B;  // AND_Gate AND32, 32 bits wide
  assign OR32_out = A | B;  // OR_Gate OR32, 32 bits wide
  assign NOR32_out = ~(A | B);  // NOR_Gate NOR32, 32 bits wide
  assign XOR32_out = A ^ B;  // XOR_Gate XOR32, 32 bits wide
  Multiplexer #(.select(2), .width(32)) multiplexer_1 (
    .in0(notequal32_out_3), .in1(equal32_output), .in2(lessthan32_out_2), .in3(greaterthan32_out_2),
    .out(multiplexer_1_out), .sel(Op[2:1]));  // open: en
  Multiplexer #(.select(2), .width(32)) multiplexer_2 (
    .in0(AND32_out), .in1(OR32_out), .in2(XOR32_out), .in3(NOR32_out), .out(multiplexer_2_out), .sel(Op[2:1]));  // open: en
  Multiplexer #(.width(32)) multiplexer_3 (
    .in0(shifter32_output), .in1(add_sub32_output), .out(multiplexer_3_out), .sel(Op[1]));  // open: en
  Multiplexer #(.width(32)) multiplexer_4 (
    .in0(multiplexer_2_out), .in1(multiplexer_1_out), .out(multiplexer_4_out), .sel(Op[0]));  // open: en
  Multiplexer #(.width(32)) multiplexer_5 (
    .in0(multiplexer_3_out), .in1(multiplexer_4_out), .out(Output), .sel(Op[3]));  // open: en
endmodule

module EQUAL32 (
  input  [31:0] A,
  input  [31:0] B,
  output [31:0] \output 
);

  wire and_1_out;
  wire [31:0] xnor_1_out;

  assign xnor_1_out = ~(A ^ B);  // XNOR_Gate xnor_1, 32 bits wide
  and and_1 (and_1_out, xnor_1_out[0], xnor_1_out[1], xnor_1_out[2], xnor_1_out[3], xnor_1_out[4], xnor_1_out[5], xnor_1_out[6], xnor_1_out[7], xnor_1_out[8], xnor_1_out[9], xnor_1_out[10], xnor_1_out[11], xnor_1_out[12], xnor_1_out[13], xnor_1_out[14], xnor_1_out[15], xnor_1_out[16], xnor_1_out[17], xnor_1_out[18], xnor_1_out[19], xnor_1_out[20], xnor_1_out[21], xnor_1_out[22], xnor_1_out[23], xnor_1_out[24], xnor_1_out[25], xnor_1_out[26], xnor_1_out[27], xnor_1_out[28], xnor_1_out[29], xnor_1_out[30], xnor_1_out[31]);
  assign \output  = {{31{1'b0}}, and_1_out};  // Bit_Extender bit_extender_1
endmodule

module NOTEQUAL32 (
  input  [31:0] A,
  input  [31:0] B,
  output [31:0] out_3
);

  wire [0:0] equal_output;

  EQUAL32 equal (.A(A), .B(B), .\output ({out_3[31:1], equal_output[0]}));
  not not_1 (out_3[0], equal_output[0]);
endmodule

module GREATERTHAN32 (
  input  [31:0] in_1,
  output [31:0] out_2
);

  wire and_1_out, and_2_out, not_1_out, xnor_1_out;
  wire [30:0] bit_extender_1_out, xnor_2_out;

  assign bit_extender_1_out = {{30{1'b0}}, 1'b0};  // Bit_Extender bit_extender_1
  xnor xnor_1 (xnor_1_out, in_1[31], 1'b0);
  assign xnor_2_out = ~(in_1[30:0] ^ bit_extender_1_out);  // XNOR_Gate xnor_2, 31 bits wide
  not not_1 (not_1_out, and_1_out);
  and and_1 (and_1_out, xnor_2_out[0], xnor_2_out[1], xnor_2_out[2], xnor_2_out[3], xnor_2_out[4], xnor_2_out[5], xnor_2_out[6], xnor_2_out[7], xnor_2_out[8], xnor_2_out[9], xnor_2_out[10], xnor_2_out[11], xnor_2_out[12], xnor_2_out[13], xnor_2_out[14], xnor_2_out[15], xnor_2_out[16], xnor_2_out[17], xnor_2_out[18], xnor_2_out[19], xnor_2_out[20], xnor_2_out[21], xnor_2_out[22], xnor_2_out[23], xnor_2_out[24], xnor_2_out[25], xnor_2_out[26], xnor_2_out[27], xnor_2_out[28], xnor_2_out[29], xnor_2_out[30]);
  and and_2 (and_2_out, xnor_1_out, not_1_out);
  assign out_2 = {{31{1'b0}}, and_2_out};  // Bit_Extender bit_extender_2
endmodule

module LESSTHAN32 (
  input  [31:0] A,
  output [31:0] out_2
);

  wire [0:0] greaterthan_out_2;

  GREATERTHAN32 greaterthan (.in_1(A), .out_2({out_2[31:1], greaterthan_out_2[0]}));
  not not_1 (out_2[0], greaterthan_out_2[0]);
endmodule

module ADDSUB32 (
  input  [31:0] A,
  input  in_2,
  input  [31:0] B,
  output [31:0] \output ,
  output out_5
);

  wire [31:0] bit_extender_1_out, xor_1_out;

  assign bit_extender_1_out = {{31{in_2}}, in_2};  // Bit_Extender bit_extender_1
  assign xor_1_out = bit_extender_1_out ^ B;  // XOR_Gate xor_1, 32 bits wide
  ADD32 adder (.A(A), .carry(in_2), .B(xor_1_out), .overflow(out_5), .out_4(\output ));
endmodule

module SHIFTER32 (
  input  Cin,
  input  [31:0] A,
  input  [4:0] shamt,
  input  [1:0] cntrl,
  output [31:0] \output 
);

  wire [31:0] lessthan_output, multiplexer_1_out, multiplexer_2_out, multiplexer_3_out, not_1_out, not_2_out;

  Multiplexer #(.width(32)) multiplexer_1 (
    .in0({A[0], A[1], A[2], A[3], A[4], A[5], A[6], A[7], A[8], A[9], A[10], A[11], A[12], A[13], A[14], A[15], A[16], A[17], A[18], A[19], A[20], A[21], A[22], A[23], A[24], A[25], A[26], A[27], A[28], A[29], A[30], A[31]}),
    .in1(not_1_out), .out(multiplexer_1_out), .sel(A[31]));  // open: en
  assign not_1_out = ~{A[0], A[1], A[2], A[3], A[4], A[5], A[6], A[7], A[8], A[9], A[10], A[11], A[12], A[13], A[14], A[15], A[16], A[17], A[18], A[19], A[20], A[21], A[22], A[23], A[24], A[25], A[26], A[27], A[28], A[29], A[30], A[31]};  // NOT_Gate not_1, 32 bits wide
  Multiplexer #(.select(2), .width(32)) multiplexer_2 (
    .in0(A), .in1(A),
    .in2({A[0], A[1], A[2], A[3], A[4], A[5], A[6], A[7], A[8], A[9], A[10], A[11], A[12], A[13], A[14], A[15], A[16], A[17], A[18], A[19], A[20], A[21], A[22], A[23], A[24], A[25], A[26], A[27], A[28], A[29], A[30], A[31]}),
    .in3(multiplexer_1_out), .out(multiplexer_2_out), .sel(cntrl));  // open: en
  leftshift_main lessthan (.A(multiplexer_2_out), .C(Cin), .\input (shamt), .\output (lessthan_output));
  assign not_2_out = ~{lessthan_output[0], lessthan_output[1], lessthan_output[2], lessthan_output[3], lessthan_output[4], lessthan_output[5], lessthan_output[6], lessthan_output[7], lessthan_output[8], lessthan_output[9], lessthan_output[10], lessthan_output[11], lessthan_output[12], lessthan_output[13], lessthan_output[14], lessthan_output[15], lessthan_output[16], lessthan_output[17], lessthan_output[18], lessthan_output[19], lessthan_output[20], lessthan_output[21], lessthan_output[22], lessthan_output[23], lessthan_output[24], lessthan_output[25], lessthan_output[26], lessthan_output[27], lessthan_output[28], lessthan_output[29], lessthan_output[30], lessthan_output[31]};  // NOT_Gate not_2, 32 bits wide
  Multiplexer #(.width(32)) multiplexer_3 (
    .in0({lessthan_output[0], lessthan_output[1], lessthan_output[2], lessthan_output[3], lessthan_output[4], lessthan_output[5], lessthan_output[6], lessthan_output[7], lessthan_output[8], lessthan_output[9], lessthan_output[10], lessthan_output[11], lessthan_output[12], lessthan_output[13], lessthan_output[14], lessthan_output[15], lessthan_output[16], lessthan_output[17], lessthan_output[18], lessthan_output[19], lessthan_output[20], lessthan_output[21], lessthan_output[22], lessthan_output[23], lessthan_output[24], lessthan_output[25], lessthan_output[26], lessthan_output[27], lessthan_output[28], lessthan_output[29], lessthan_output[30], lessthan_output[31]}),
    .in1(not_2_out), .out(multiplexer_3_out), .sel(A[31]));  // open: en
  Multiplexer #(.select(2), .width(32)) multiplexer_4 (
    .in0(lessthan_output), .in1(lessthan_output),
    .in2({lessthan_output[0], lessthan_output[1], lessthan_output[2], lessthan_output[3], lessthan_output[4], lessthan_output[5], lessthan_output[6], lessthan_output[7], lessthan_output[8], lessthan_output[9], lessthan_output[10], lessthan_output[11], lessthan_output[12], lessthan_output[13], lessthan_output[14], lessthan_output[15], lessthan_output[16], lessthan_output[17], lessthan_output[18], lessthan_output[19], lessthan_output[20], lessthan_output[21], lessthan_output[22], lessthan_output[23], lessthan_output[24], lessthan_output[25], lessthan_output[26], lessthan_output[27], lessthan_output[28], lessthan_output[29], lessthan_output[30], lessthan_output[31]}),
    .in3(multiplexer_3_out), .out(\output ), .sel(cntrl));  // open: en
endmodule
