// Logisim project adder.circ as structural Verilog: 6 circuits, main circuit ADD32
module ADD32 (
  input  [31:0] A,
  input  carry,
  input  [31:0] B,
  output [31:0] out_4,
  output overflow
);

  wire n1_bit_1_cout, n1_bit_2_cout, n2_bit_1_cout, n4_bit_1_cout, n8_bit_1_cout, n16_bit_1_cout;

  _16_bit u_16_bit_1 (.A(A[15:0]), .Cin(carry), .B(B[15:0]), .Sum(out_4[15:0]), .Cout(n16_bit_1_cout));
  _8_bit u_8_bit_1 (.A(A[23:16]), .Cin(n16_bit_1_cout), .B(B[23:16]), .out_4(out_4[23:16]), .Cout(n8_bit_1_cout));
  _4_bit u_4_bit_1 (.A(A[27:24]), .Cin(n8_bit_1_cout), .B(B[27:24]), .sum(out_4[27:24]), .Cout(n4_bit_1_cout));
  _2_bit u_2_bit_1 (.A(A[29:28]), .Cin(n4_bit_1_cout), .B(B[29:28]), .Sum(out_4[29:28]), .Cout(n2_bit_1_cout));
  _1_bit u_1_bit_1 (.A(A[30]), .B(n2_bit_1_cout), .Cin(B[30]), .sum(out_4[30]), .Cout(n1_bit_1_cout));
  _1_bit u_1_bit_2 (.A(A[31]), .B(n1_bit_1_cout), .Cin(B[31]), .sum(out_4[31]), .Cout(n1_bit_2_cout));
  xor xor_1 (overflow, n1_bit_1_cout, n1_bit_2_cout);
endmodule

module _1_bit (
  input  A,
  input  B,
  input  Cin,
  output sum,
  output Cout
);

  wire and_1_out, and_2_out, xor_1_out;

  xor xor_1 (xor_1_out, A, B);
  and and_1 (and_1_out, A, B);
  xor xor_2 (sum, xor_1_out, Cin);
  and and_2 (and_2_out, xor_1_out, Cin);
  or or_1 (Cout, and_2_out, and_1_out);
endmodule

module _2_bit (
  input  [1:0] A,
  input  Cin,
  input  [1:0] B,
  output [1:0] Sum,
  output Cout
);

  wire LSB_cout;

  _1_bit LSB (.A(A[0]), .B(B[0]), .Cin(Cin), .sum(Sum[0]), .Cout(LSB_cout));
  _1_bit MSB (.A(A[1]), .B(B[1]), .Cin(LSB_cout), .sum(Sum[1]), .Cout(Cout));
endmodule

module _4_bit (
  input  [3:0] A,
  input  Cin,
  input  [3:0] B,
  output [3:0] sum,
  output Cout
);

  wire LSB_cout;

  _2_bit LSB (.A(A[1:0]), .Cin(Cin), .B(B[1:0]), .Sum(sum[1:0]), .Cout(LSB_cout));
  _2_bit MSB (.A(A[3:2]), .Cin(LSB_cout), .B(B[3:2]), .Sum(sum[3:2]), .Cout(Cout));
endmodule

module _8_bit (
  input  [7:0] A,
  input  Cin,
  input  [7:0] B,
  output [7:0] out_4,
  output Cout
);

  wire LSB_cout;

  _4_bit LSB (.A(A[3:0]), .Cin(Cin), .B(B[3:0]), .sum(out_4[3:0]), .Cout(LSB_cout));
  _4_bit MSB (.A(A[7:4]), .Cin(LSB_cout), .B(B[7:4]), .sum(out_4[7:4]), .Cout(Cout));
endmodule

module _16_bit (
  input  [15:0] A,
  input  Cin,
  input  [15:0] B,
  output [15:0] Sum,
  output Cout
);

  wire LSB_cout;

  _8_bit LSB (.A(A[7:0]), .Cin(Cin), .B(B[7:0]), .out_4(Sum[7:0]), .Cout(LSB_cout));
  _8_bit MSB (.A(A[15:8]), .Cin(LSB_cout), .B(B[15:8]), .out_4(Sum[15:8]), .Cout(Cout));
endmodule
