// Logisim project leftshift.circ as structural Verilog: 6 circuits, main circuit main
module main (
  input  [31:0] A,
  input  C,
  input  [4:0] \input ,
  output [31:0] \output 
);

  wire [31:0] multiplexer_1_out, multiplexer_2_out, multiplexer_3_out, multiplexer_4_out, n1_1_out_3,
       n2_1_out_3, n4_1_out_3, n8_1_out_3, n16_1_out_3;

  Multiplexer #(.width(32)) multiplexer_1 (
    .in0(A), .in1(n16_1_out_3), .out(multiplexer_1_out), .sel(\input [4]));  // open: en
  _16 u_16_1 (.A(A), .C(C), .out_3(n16_1_out_3));
  _8 u_8_1 (.A(multiplexer_1_out), .C(C), .out_3(n8_1_out_3));
  Multiplexer #(.width(32)) multiplexer_2 (
    .in0(multiplexer_1_out), .in1(n8_1_out_3), .out(multiplexer_2_out), .sel(\input [3]));  // open: en
  _4 u_4_1 (.A(multiplexer_2_out), .in_2(C), .out_3(n4_1_out_3));
  Multiplexer #(.width(32)) multiplexer_3 (
    .in0(multiplexer_2_out), .in1(n4_1_out_3), .out(multiplexer_3_out), .sel(\input [2]));  // open: en
  _2 u_2_1 (.A(multiplexer_3_out), .C(C), .out_3(n2_1_out_3));
  Multiplexer #(.width(32)) multiplexer_4 (
    .in0(multiplexer_3_out), .in1(n2_1_out_3), .out(multiplexer_4_out), .sel(\input [1]));  // open: en
  _1 u_1_1 (.A(multiplexer_4_out), .C(C), .out_3(n1_1_out_3));
  Multiplexer #(.width(32)) multiplexer_5 (
    .in0(multiplexer_4_out), .in1(n1_1_out_3), .out(\output ), .sel(\input [0]));  // open: en
endmodule

module _1 (
  input  [31:0] A,
  input  C,
  output [31:0] out_3
);


  assign out_3 = {A[30:0], C};
endmodule

module _2 (
  input  [31:0] A,
  input  C,
  output [31:0] out_3
);


  assign out_3 = {A[29:0], {2{C}}};
endmodule

module _4 (
  input  [31:0] A,
  input  in_2,
  output [31:0] out_3
);


  assign out_3 = {A[27:0], {4{in_2}}};
endmodule

module _8 (
  input  [31:0] A,
  input  C,
  output [31:0] out_3
);


  assign out_3 = {A[23:0], {8{C}}};
endmodule

module _16 (
  input  [31:0] A,
  input  C,
  output [31:0] out_3
);


  assign out_3 = {A[15:0], {16{C}}};
endmodule
